# Fritzing sketch stepper_motor (saved by Fritzing 1.0.7)

parts:
  STEP_17HS_1 = Stepper Motor - Bipolar
  VMOT_12V = 2.1mm DC Barrel Jack
  S_1 = Toggle Switch [package=THT]
  TMC2209_Stepper_Motor_Driver1 = Adafruit TMC2209 Stepper Motor Driver [part_number=#6121]
  J3 = Camdenboss CTB0158-12 [part_number=CTB0158-12 package=THT]
  Arduino_Mega_1 = Arduino Mega 2560 (Rev3)

nets:
  N1: STEP_17HS_1.A, TMC2209_Stepper_Motor_Driver1.OUT2B
  N2: STEP_17HS_1.C, TMC2209_Stepper_Motor_Driver1.OUT2A
  N3: STEP_17HS_1.B, TMC2209_Stepper_Motor_Driver1.OUT1A
  N4: STEP_17HS_1.D, TMC2209_Stepper_Motor_Driver1.OUT1B
  N5: VMOT_12V.center, S_1.L2
  GND: VMOT_12V.switch, TMC2209_Stepper_Motor_Driver1.GND, J3.terminal_10, Arduino_Mega_1.GND
  N6: VMOT_12V.sleeve, J3.pin11
  N7: S_1.L1, J3.pin12
  N8: TMC2209_Stepper_Motor_Driver1.VMOTOR, J3.terminal_9
  VDD: TMC2209_Stepper_Motor_Driver1.VDD, Arduino_Mega_1.5V
  N9: TMC2209_Stepper_Motor_Driver1.DIR, Arduino_Mega_1.D3_PWM
  N10: TMC2209_Stepper_Motor_Driver1.STEP, Arduino_Mega_1.D2_PWM

// code stored in the sketch: Sketch1.ino
#define STEP_PIN 2
#define DIR_PIN 3

void setup() {
  pinmode(STEP_PIN, OUTPUT);
  pinmode(DIR_PIN, OUTPUT);

  digitalWrite(DIR_PIN, HIGH);
}
void loop() {
  digitalWrite(STEP_PIN, HIGH);
  delayMicroseconds(500);

  digitalWrite(STEP_PIN, LOW);
  delayMicroseconds(500);
}
